// Digital circuit 3-8译码器.dig as structural Verilog
module \_3_8译码器  (
  input  A0,
  input  A1,
  input  A2,
  output R0,
  output R1,
  output R2,
  output R3,
  output R4,
  output R5,
  output R6,
  output R7
);

  wire not_1_out, not_2_out, not_3_out;

  not not_1 (not_1_out, A2);
  not not_2 (not_2_out, A1);
  not not_3 (not_3_out, A0);
  and and_1 (R0, not_3_out, not_2_out, not_1_out);
  and and_2 (R1, A0, not_2_out, not_1_out);
  and and_3 (R2, not_3_out, A1, not_1_out);
  and and_4 (R3, A0, A1, not_1_out);
  and and_5 (R4, not_3_out, not_2_out, A2);
  and and_6 (R5, A0, not_2_out, A2);
  and and_7 (R6, not_3_out, A1, A2);
  and and_8 (R7, A0, A1, A2);
endmodule
