// Digital circuit 8位减法电路.dig as structural Verilog
module \_8位减法电路  (
  input  [7:0] A,
  input  [7:0] B,
  output [7:0] S,
  output C
);

  wire \减法电路_1_c , \减法电路_2_c , \减法电路_3_c , \减法电路_4_c , \减法电路_5_c , \减法电路_6_c , \减法电路_7_c ;

  \减法电路  \u_减法电路_1  (.A(A[0]), .B(B[0]), .C_in(1'b0), .S(S[0]), .C(\减法电路_1_c ));
  \减法电路  \u_减法电路_2  (.A(A[1]), .B(B[1]), .C_in(\减法电路_1_c ), .S(S[1]), .C(\减法电路_2_c ));
  \减法电路  \u_减法电路_3  (.A(A[2]), .B(B[2]), .C_in(\减法电路_2_c ), .S(S[2]), .C(\减法电路_3_c ));
  \减法电路  \u_减法电路_4  (.A(A[3]), .B(B[3]), .C_in(\减法电路_3_c ), .S(S[3]), .C(\减法电路_4_c ));
  \减法电路  \u_减法电路_5  (.A(A[4]), .B(B[4]), .C_in(\减法电路_4_c ), .S(S[4]), .C(\减法电路_5_c ));
  \减法电路  \u_减法电路_6  (.A(A[5]), .B(B[5]), .C_in(\减法电路_5_c ), .S(S[5]), .C(\减法电路_6_c ));
  \减法电路  \u_减法电路_7  (.A(A[6]), .B(B[6]), .C_in(\减法电路_6_c ), .S(S[6]), .C(\减法电路_7_c ));
  \减法电路  \u_减法电路_8  (.A(A[7]), .B(B[7]), .C_in(\减法电路_7_c ), .S(S[7]), .C(C));

  // Other names for the same wires on the sheet: A_0 = A[0]; A_1 = A[1]; A_2 = A[2]; A_3 = A[3]; A_4 = A[4];
  //   A_5 = A[5]; A_6 = A[6]; A_7 = A[7]; B_0 = B[0]; B_1 = B[1]; B_2 = B[2]; B_3 = B[3]; B_4 = B[4]; B_5 = B[5];
  //   B_6 = B[6]; B_7 = B[7]; S_0 = S[0]; S_1 = S[1]; S_2 = S[2]; S_3 = S[3]; S_4 = S[4]; S_5 = S[5]; S_6 = S[6];
  //   S_7 = S[7]
endmodule
