// Digital circuit ALU+寄存器-加减指令-hlat-jmp-cmp.dig as structural Verilog
module \ALU_寄存器_加减指令_hlat_jmp_cmp  (
  output [15:0] O,
  output [15:0] S,
  output CMP_O
);

  wire ALU_zf, button_1_out, Clock, CMP_en, D_ld, D_out, D_str, hlat, PC_jmp, R_en, R_out;
  wire [2:0] \pc计数器_jmp_1_s ;
  wire [15:0] multiplexer_1_out, multiplexer_2_out, S_out, \指令_d ;

  Button button_1 (.out(button_1_out));
  and and_1 (Clock, button_1_out, hlat);
  Register register_1 (.D(ALU_zf), .C(Clock), .en(CMP_en), .Q(CMP_O));
  \PC计数器_jmp  #(.generic("Bits := 3 ;")) \pc计数器_jmp_1  (
    .A(Clock), .PC_in(S_out[2:0]), .PC_SW(PC_jmp), .S(\pc计数器_jmp_1_s ));  // open: T
  Register #(.Bits(16)) register_2 (.D(S_out), .C(Clock), .en(R_en), .Q(O));
  EEPROMDualPort #(.AddrBits(3), .Bits(16)) \u_数据  (
    .A(\pc计数器_jmp_1_s ), .Din(S_out), .str(D_str), .C(Clock), .ld(D_ld), .D(S));
  EEPROMDualPort #(.AddrBits(3), .Bits(16)) \u_指令  (
    .A(\pc计数器_jmp_1_s ), .Din({16{1'b0}}), .str(1'b0), .C(Clock), .ld(1'b1),
    .D({\指令_d [15:10], CMP_en, PC_jmp, R_out, D_out, D_ld, D_str, R_en, hlat, \指令_d [1:0]}));
  Multiplexer #(.Bits(16)) multiplexer_1 (.sel(R_out), .in_0(O), .in_1({16{1'b0}}), .out(multiplexer_1_out));
  Multiplexer #(.Bits(16)) multiplexer_2 (.sel(D_out), .in_0(S), .in_1({16{1'b0}}), .out(multiplexer_2_out));
  // ALU电路_cmp #(.generic("Bits := 16 ;")) alu电路_cmp_1: pin names not known; wires that end beside it: multiplexer_1_out, multiplexer_2_out, 1'b0, \指令_d [1:0], S_out, ALU_zf

  // Other names for the same wires on the sheet: CMP_out = CMP_O

  // Notes on the sheet:
  //   contents of 数据 (hex, n*v repeats v):
  //   f,3,2,10
  //   contents of 指令 (hex, n*v repeats v):
  //   ac,2c,2d,224
endmodule
