// Digital circuit ALU+寄存器-加减指令-hlat-自动4个控制.dig as structural Verilog
module \ALU_寄存器_加减指令_hlat_自动4个控制  (
  output [15:0] O,
  output [15:0] S
);

  wire button_1_out, Clock, D_ld, D_out, D_str, hlat, R_en;
  wire [2:0] \pc计数器_1_s ;
  wire [15:0] multiplexer_1_out, S_out, \指令_d ;

  Button button_1 (.out(button_1_out));
  and and_1 (Clock, button_1_out, hlat);
  \PC计数器  #(.generic("Bits := 3;")) \pc计数器_1  (.A(Clock), .S(\pc计数器_1_s ));  // open: T
  Register #(.Bits(16)) register_1 (.D(S_out), .C(Clock), .en(R_en), .Q(O));
  EEPROMDualPort #(.AddrBits(3), .Bits(16)) \u_数据  (
    .A(\pc计数器_1_s ), .Din(S_out), .str(D_str), .C(Clock), .ld(D_ld), .D(S));
  EEPROMDualPort #(.AddrBits(3), .Bits(16)) \u_指令  (
    .A(\pc计数器_1_s ), .Din({16{1'b0}}), .str(1'b0), .C(Clock), .ld(1'b1),
    .D({\指令_d [15:7], D_out, D_ld, D_str, R_en, hlat, \指令_d [1:0]}));
  Multiplexer #(.Bits(16)) multiplexer_1 (.sel(D_out), .in_0(S), .in_1({16{1'b0}}), .out(multiplexer_1_out));
  // ALU电路 #(.generic("Bits := 16;")) alu电路_1: pin names not known; wires that end beside it: O, multiplexer_1_out, 1'b0, \指令_d [1:0], S_out

  // Notes on the sheet:
  //   contents of 数据 (hex, n*v repeats v):
  //   50,14,1e,28,1,1f
  //   contents of 指令 (hex, n*v repeats v):
  //   2c,2c,2d,2d,2c,54
endmodule
