// Digital circuit ALU+寄存器-加减指令-hlat.dig as structural Verilog
module \ALU_寄存器_加减指令_hlat  (
  output [15:0] O,
  output [15:0] S
);

  wire button_1_out, Clock, hlat;
  wire [2:0] \pc计数器_1_s ;
  wire [15:0] \alu电路_1_p5 , \指令_d ;

  Button button_1 (.out(button_1_out));
  and and_1 (Clock, button_1_out, hlat);
  \PC计数器  #(.generic("Bits := 3;")) \pc计数器_1  (.A(Clock), .S(\pc计数器_1_s ));  // open: T
  Register #(.Bits(16)) register_1 (.D(\alu电路_1_p5 ), .C(Clock), .en(1'b1), .Q(O));
  EEPROMDualPort #(.AddrBits(3), .Bits(16)) \u_数据  (
    .A(\pc计数器_1_s ), .Din({16{1'b0}}), .str(1'b0), .C(Clock), .ld(1'b1), .D(S));
  EEPROMDualPort #(.AddrBits(3), .Bits(16)) \u_指令  (
    .A(\pc计数器_1_s ), .Din({16{1'b0}}), .str(1'b0), .C(Clock), .ld(1'b1), .D({\指令_d [15:3], hlat, \指令_d [1:0]}));
  // ALU电路 #(.generic("Bits := 16;")) alu电路_1: pin names not known; wires that end beside it: O, S, 1'b0, \指令_d [1:0], \alu电路_1_p5 

  // Notes on the sheet:
  //   contents of 数据 (hex, n*v repeats v):
  //   50,14,1e,28,1
  //   contents of 指令 (hex, n*v repeats v):
  //   4,4,5,5,4
endmodule
