// Digital circuit ALU+寄存器-加减指令.dig as structural Verilog
module \ALU_寄存器_加减指令  (
  output [15:0] O,
  output [15:0] S
);

  wire Clock;
  wire [1:0] \pc计数器_1_p2 ;
  wire [15:0] \alu电路_1_p5 , eepromdualport_2_d;

  Button button_1 (.out(Clock));
  // PC计数器 #(.generic("Bits := 2;")) pc计数器_1: pin names not known; wires that end beside it: Clock, \pc计数器_1_p2 
  Register #(.Bits(16)) register_1 (.D(\alu电路_1_p5 ), .C(Clock), .en(1'b1), .Q(O));
  EEPROMDualPort #(.Bits(16)) eepromdualport_1 (
    .A(\pc计数器_1_p2 ), .Din({16{1'b0}}), .str(1'b0), .C(Clock), .ld(1'b1), .D(S));
  EEPROMDualPort #(.Bits(16)) eepromdualport_2 (
    .A(\pc计数器_1_p2 ), .Din({16{1'b0}}), .str(1'b0), .C(Clock), .ld(1'b1), .D(eepromdualport_2_d));
  // ALU电路 #(.generic("Bits := 16;")) alu电路_1: pin names not known; wires that end beside it: O, S, 1'b0, eepromdualport_2_d[1:0], \alu电路_1_p5 

  // Notes on the sheet:
  //   contents of eepromdualport_1 (hex, n*v repeats v):
  //   50,14,1e,28
  //   contents of eepromdualport_2 (hex, n*v repeats v):
  //   0,0,1,1
endmodule
