// Digital circuit ALU+寄存器-自己内存.dig as structural Verilog
module \ALU_寄存器_自己内存  (
  input  [15:0] D_in,
  input  str,
  input  ld,
  input  en,
  output [15:0] O,
  output [15:0] S
);

  wire button_1_out;
  wire [2:0] \pc计数器_1_s ;
  wire [15:0] \alu电路_1_p5 ;

  \PC计数器  #(.generic("Bits := 3;")) \pc计数器_1  (.A(button_1_out), .S(\pc计数器_1_s ));  // open: T
  Button button_1 (.out(button_1_out));
  Register #(.Bits(16)) register_1 (.D(\alu电路_1_p5 ), .C(button_1_out), .en(en), .Q(O));
  \寄存器实现16BitX8内存  \u_寄存器实现16bitx8内存_1  (.A(\pc计数器_1_s ), .D_in(D_in), .str(str), .C(button_1_out), .ld(ld), .D(S));
  // ALU电路 #(.generic("Bits := 16;")) alu电路_1: pin names not known; wires that end beside it: O, S, 1'b0, 2'b00, \alu电路_1_p5 
endmodule
