// Digital circuit ALU+寄存器.dig as structural Verilog
module \ALU_寄存器  (
  output [15:0] O,
  output [15:0] S
);

  wire \pc计数器_1_p1 ;
  wire [1:0] \pc计数器_1_p2 ;
  wire [15:0] \alu电路_1_p5 ;

  // PC计数器 #(.generic("Bits := 2;")) pc计数器_1: pin names not known; wires that end beside it: \pc计数器_1_p1 , \pc计数器_1_p2 
  Button button_1 (.out(\pc计数器_1_p1 ));
  Register #(.Bits(16)) register_1 (.D(\alu电路_1_p5 ), .C(\pc计数器_1_p1 ), .en(1'b1), .Q(O));
  EEPROMDualPort #(.Bits(16)) eepromdualport_1 (
    .A(\pc计数器_1_p2 ), .Din({16{1'b0}}), .str(1'b0), .C(\pc计数器_1_p1 ), .ld(1'b1), .D(S));
  // ALU电路 #(.generic("Bits := 16;")) alu电路_1: pin names not known; wires that end beside it: O, S, 1'b0, 2'b00, \alu电路_1_p5 

  // Notes on the sheet:
  //   contents of eepromdualport_1 (hex, n*v repeats v):
  //   a,14,1e,28
endmodule
