// Digital circuit ALU电路-cmp.dig as structural Verilog
module \ALU电路_cmp  (
  input  [7:0] A,
  input  [7:0] B,
  input  C_in,
  input  [1:0] Sel,
  output [7:0] S,
  output C_out,
  output ZF
);

  wire add_1_c_o, sub_1_c_o;
  wire [7:0] add_1_s, and_1_out, or_1_out, sub_1_s;

  Add #(.Bits(8), .generic("this.Bits = args.Bits;")) add_1 (.a(A), .b(B), .c_i(C_in), .s(add_1_s), .c_o(add_1_c_o));
  Sub #(.Bits(8), .generic("this.Bits = args.Bits;")) sub_1 (.a(A), .b(B), .c_i(C_in), .s(sub_1_s), .c_o(sub_1_c_o));
  assign and_1_out = A & B;  // And and_1, 8 bits wide
  assign or_1_out = A | B;  // Or or_1, 8 bits wide
  Comparator #(.generic("this.Bits = args.Bits;")) comparator_1 (.a(A), .b(B), .eq(ZF));  // open: gt, lt
  Multiplexer #(.Selector_Bits(2), .Bits(8), .generic("this.Bits = args.Bits;")) multiplexer_1 (
    .sel(Sel), .in_0(add_1_s), .in_1(sub_1_s), .in_2(and_1_out), .in_3(or_1_out), .out(S));
  Multiplexer multiplexer_2 (.sel(Sel[0]), .in_0(add_1_c_o), .in_1(sub_1_c_o), .out(C_out));
endmodule

/* Code that sets the parameters or builds the circuit:
Bits := 16 ;
*/
