// Digital circuit PC计数器-jmp.dig as structural Verilog
module \PC计数器_jmp  (
  input  A,
  input  PC_in,
  input  PC_SW,
  output [2:0] S,
  output T
);

  wire [1:0] add_1_s, multiplexer_1_out;

  Multiplexer #(.generic("this.Bits = args.Bits;")) multiplexer_1 (
    .sel(PC_SW), .in_0(add_1_s), .in_1(PC_in), .out(multiplexer_1_out));
  Register #(.Bits(2), .generic("this.Bits = args.Bits;")) register_1 (
    .D(multiplexer_1_out), .C(A), .en(1'b1), .Q(S[1:0]));
  Add #(.Bits(2), .generic("this.Bits = args.Bits;")) add_1 (.a(S[1:0]), .b(2'b01), .c_i(1'b0), .s(add_1_s), .c_o(T));
  // Pins of 2 and 3 bits meet at S
endmodule

/* Code that sets the parameters or builds the circuit:
Bits := 3 ;
*/
