// Digital circuit PC计数器.dig as structural Verilog
module \PC计数器  (
  input  A,
  output [2:0] S,
  output T
);

  wire [1:0] add_1_s;

  Register #(.Bits(2), .generic("this.Bits = args.Bits;")) register_1 (.D(add_1_s), .C(A), .en(1'b1), .Q(S[1:0]));
  Add #(.Bits(2), .generic("this.Bits = args.Bits;")) add_1 (.a(S[1:0]), .b(2'b01), .c_i(1'b0), .s(add_1_s), .c_o(T));
  // Pins of 2 and 3 bits meet at S
endmodule

/* Code that sets the parameters or builds the circuit:
Bits := 3 ;
*/
