// Digital circuit SR锁存器.dig as structural Verilog
module \SR锁存器  (
  input  S,
  input  R,
  output Q,
  output Q_2
);

  nand nand_1 (Q, S, Q_2);
  nand nand_2 (Q_2, Q, R);

  // Notes on the sheet:
  //   S: default 1
  //   R: default 1
endmodule
