// Digital circuit 减法电路.dig as structural Verilog
module \减法电路  (
  input  A,
  input  B,
  input  C_in,
  output S,
  output C
);

  wire \半减法电路_1_c , \半减法电路_1_s , \半减法电路_2_c ;

  \半减法电路  \u_半减法电路_1  (.A(A), .B(B), .S(\半减法电路_1_s ), .C(\半减法电路_1_c ));
  \半减法电路  \u_半减法电路_2  (.A(\半减法电路_1_s ), .B(C_in), .S(S), .C(\半减法电路_2_c ));
  or or_1 (C, \半减法电路_2_c , \半减法电路_1_c );
endmodule
