// Digital circuit 加法器.dig as structural Verilog
module \加法器  (
  input  A,
  input  B,
  input  C_in,
  output S,
  output C_out
);

  wire \半加器_1_c进 , \半加器_1_s , \半加器_2_c进 ;

  \半加器  \u_半加器_1  (.A(A), .B(B), .S(\半加器_1_s ), .\C进 (\半加器_1_c进 ));
  \半加器  \u_半加器_2  (.A(C_in), .B(\半加器_1_s ), .S(S), .\C进 (\半加器_2_c进 ));
  or or_1 (C_out, \半加器_2_c进 , \半加器_1_c进 );
endmodule
