// Digital circuit 半减法电路.dig as structural Verilog
module \半减法电路  (
  input  A,
  input  B,
  output S,
  output C
);

  wire not_1_out;

  not not_1 (not_1_out, A);
  xor xor_1 (S, A, B);
  and and_1 (C, B, not_1_out);
endmodule
