// Digital circuit 寄存器.dig as structural Verilog
module \寄存器  (
  input  [3:0] D,
  input  C,
  input  en,
  output [3:0] out_2
);

  wire and_1_out;

  and and_1 (and_1_out, C, en);
  \D锁存器  \d锁存器_1  (.D(D[0]), .en(and_1_out), .Q(out_2[0]));  // open: Q_2
  \D锁存器  \d锁存器_2  (.D(D[1]), .en(and_1_out), .Q(out_2[1]));  // open: Q_2
  \D锁存器  \d锁存器_3  (.D(D[2]), .en(and_1_out), .Q(out_2[2]));  // open: Q_2
  \D锁存器  \d锁存器_4  (.D(D[3]), .en(and_1_out), .Q(out_2[3]));  // open: Q_2
endmodule
