// Digital circuit 寄存器实现16BitX8内存.dig as structural Verilog
module \寄存器实现16BitX8内存  (
  input  [2:0] A,
  input  [15:0] D_in,
  input  str,
  input  C,
  input  ld,
  output [15:0] D
);

  wire A_0, A_1, A_2, A_3, A_4, A_5, A_6, A_7, and_1_out, and_2_out, and_3_out, and_4_out, and_5_out,
       and_6_out, and_7_out, and_8_out;
  wire [15:0] D_0, D_1, D_2, D_3, D_4, D_5, D_6, D_7, multiplexer_1_out;

  \_3_8译码器  \_3_8译码器_1  (
    .A0(A[0]), .A1(A[1]), .A2(A[2]), .R0(A_0), .R1(A_1), .R2(A_2), .R3(A_3), .R4(A_4), .R5(A_5), .R6(A_6),
    .R7(A_7));
  and and_1 (and_1_out, A_0, str);
  and and_2 (and_2_out, A_1, str);
  and and_3 (and_3_out, A_2, str);
  and and_4 (and_4_out, A_3, str);
  Register #(.Bits(16)) register_1 (.D(D_in), .C(C), .en(and_1_out), .Q(D_0));
  Register #(.Bits(16)) register_2 (.D(D_in), .C(C), .en(and_2_out), .Q(D_1));
  Register #(.Bits(16)) register_3 (.D(D_in), .C(C), .en(and_3_out), .Q(D_2));
  Register #(.Bits(16)) register_4 (.D(D_in), .C(C), .en(and_4_out), .Q(D_3));
  and and_5 (and_5_out, A_4, str);
  and and_6 (and_6_out, A_5, str);
  and and_7 (and_7_out, A_6, str);
  and and_8 (and_8_out, A_7, str);
  Register #(.Bits(16)) register_5 (.D(D_in), .C(C), .en(and_5_out), .Q(D_4));
  Register #(.Bits(16)) register_6 (.D(D_in), .C(C), .en(and_6_out), .Q(D_5));
  Register #(.Bits(16)) register_7 (.D(D_in), .C(C), .en(and_7_out), .Q(D_6));
  Register #(.Bits(16)) register_8 (.D(D_in), .C(C), .en(and_8_out), .Q(D_7));
  Multiplexer #(.Selector_Bits(3), .Bits(16)) multiplexer_1 (
    .sel(A), .in_0(D_0), .in_1(D_1), .in_2(D_2), .in_3(D_3), .in_4(D_4), .in_5(D_5), .in_6(D_6), .in_7(D_7),
    .out(multiplexer_1_out));
  assign D = ld ? multiplexer_1_out : 16'bz;  // Driver driver_1
endmodule
