// Digital circuit 带EN的SR锁存器.dig as structural Verilog
module \带EN的SR锁存器  (
  input  S,
  input  R,
  input  en,
  output Q,
  output Q_2
);

  wire and_1_out, and_2_out;

  and and_1 (and_1_out, S, en);
  and and_2 (and_2_out, en, R);
  nand nand_1 (Q, and_1_out, Q_2);
  nand nand_2 (Q_2, Q, and_2_out);

  // Notes on the sheet:
  //   S: default 1
  //   R: default 1
  //   en: default 1
endmodule
