// Digital circuit 简化电路表示.dig as structural Verilog
module \简化电路表示  (
  input  A,
  input  A_2,
  input  B_2,
  input  A_3,
  input  B_3,
  input  A_4,
  input  B_4,
  input  A_5,
  input  B_5,
  input  A_6,
  input  B_6,
  input  A_7,
  input  B_7,
  output B,
  output C,
  output C_2,
  output C_3,
  output out_14,
  output out_17,
  output out_20
);

  not not_1 (B, A);
  and and_1 (C, A_2, B_2);
  or or_1 (C_2, A_3, B_3);
  xor xor_1 (C_3, A_4, B_4);
  nand nand_1 (out_14, A_5, B_5);
  nor nor_1 (out_17, A_6, B_6);
  xnor xnor_1 (out_20, A_7, B_7);
endmodule
