// Digital circuit 边沿触发的D触发器.dig as structural Verilog
module \边沿触发的D触发器  (
  input  D,
  input  en,
  output Q,
  output S
);

  wire not_1_out, \改进后的带en的锁存器_1_p3 ;

  not not_1 (not_1_out, en);
  // 改进后的带EN的锁存器 改进后的带en的锁存器_1: pin names not known; wires that end beside it: D, not_1_out, \改进后的带en的锁存器_1_p3 
  // 改进后的带EN的锁存器 改进后的带en的锁存器_2: pin names not known; wires that end beside it: \改进后的带en的锁存器_1_p3 , en, Q, S
endmodule
